# Fritzing sketch UltrasonicoEsp8266 (saved by Fritzing 0.9.3b)
breadboards: 2

parts:
  U1 = ESP8266 NodeMCU LoLin module
  HC-SR04_Sensor_1 = HC-SR04 Ultrasonic Distance Sensor
  LED4 = LED - 5mm [color="Yellow (585nm)" package="5 mm [THT]"]
  LED5 = LED - 5mm [color="Red (633nm)" package="5 mm [THT]"]
  LED6 = LED - 5mm [color="Green (555nm)" package="5 mm [THT]"]
  R1 = Resistor [tolerance=±5% resistance=150 package="1206 [SMD]"]
  R2 = Resistor [tolerance=±5% resistance=150 package="1206 [SMD]"]
  R3 = Resistor [tolerance=±5% resistance=150 package="1206 [SMD]"]

nets:
  N1: U1.D1, HC-SR04_Sensor_1.TRIG
  N2: U1.D2, HC-SR04_Sensor_1.ECHO
  GND: U1.GND, HC-SR04_Sensor_1.GND, LED4.cathode, LED5.cathode, LED6.cathode
  N3: U1.D6, R1.Pin_0
  N4: U1.D7, R2.Pin_0
  N5: U1.D8, R3.Pin_0
  VIN: U1.Vin, HC-SR04_Sensor_1.VCC
  N6: LED4.anode, R2.Pin_1
  N7: LED5.anode, R1.Pin_1
  N8: LED6.anode, R3.Pin_1

custom parts:
  ESP8266 NodeMCU LoLin module: ESP8266 based NodeMCU

// code stored in the sketch: Untitled.ino
long readUltrasonicDistance(int triggerPin, int echoPin)
{
	pinMode(triggerPin, OUTPUT); //limpa o trigger (Varredura da onda)
  	digitalWrite(triggerPin, LOW);
  	delayMicroseconds(2);
  	//Ajusta o pino do trigger do sensor ultrasonico
  	//para o estado HIGH (ligado) durante 10 microsegundos
  	digitalWrite(triggerPin, HIGH);
  	delayMicroseconds(10);
  	digitalWrite(triggerPin, LOW);
  	pinMode(echoPin, INPUT);
  	//Lê o pulso refletido no pino echo e retorna o tempo da
  	//viagem sonora sound wave travel em microsegundos
  	return pulseIn(echoPin, HIGH);
}
void setup()
{
  	pinMode(0, OUTPUT);
  	Serial.begin(9600);
  	pinMode(12,OUTPUT);
    pinMode(13,OUTPUT);
    pinMode(15,OUTPUT);
  
}

void loop()
{
  	tone(0,523,1000); //soa um tom 60 (C5 = 523 Hz)
  	Serial.println(0.01723 * readUltrasonicDistance(5, 4));
  	if((0.01723 * readUltrasonicDistance(5, 4)) < 70)
    {
   		digitalWrite(12, HIGH);
      	digitalWrite(13, LOW);
      	digitalWrite(15, LOW);
    }
  	else
    {
      if((0.01723 * readUltrasonicDistance(5, 4)) < 150)
        {
        	digitalWrite(12, LOW);
      		digitalWrite(13, HIGH);
      		digitalWrite(15, LOW);
        }
      	else
      	{
      		digitalWrite(12, LOW);
      		digitalWrite(13, LOW);
      		digitalWrite(15, HIGH);
        }
  	}
  delay(10); // Wait for 1000 millisecond(s)
}
