# Fritzing sketch giroscopioModelo (saved by Fritzing 0.9.3b)
breadboards: 2

parts:
  U1 = ESP8266 NodeMCU LoLin module
  GY1 = MPU-6050 Board GY-521 [form="♀ (female)" package=THT]

nets:
  N1: U1.D1, GY1.pin3
  N2: U1.D2, GY1.pin4
  N3: U1.3V3, GY1.pin1
  N4: U1.GND, GY1.pin2

custom parts:
  ESP8266 NodeMCU LoLin module: ESP8266 based NodeMCU
  MPU-6050 Board GY-521: Acelerometro y Giroscopio MPU-6050 Board GY-521
