# Fritzing sketch giroscopioModeloI2C (saved by Fritzing 0.9.3b)
breadboards: 2

parts:
  U1 = ESP8266 NodeMCU LoLin module
  GY1 = MPU-6050 Board GY-521 [form="♀ (female)" package=THT]
  Display1 = LCD screen 16x2 IIC [part_number=101290]

nets:
  3V3: U1.D1, U1.D2, U1.3V3, GY1.pin1, GY1.pin3, GY1.pin4, Display1.VCC, Display1.SDA, Display1.SCL
  GND: U1.GND, GY1.pin2, Display1.GND

custom parts:
  ESP8266 NodeMCU LoLin module: ESP8266 based NodeMCU
  MPU-6050 Board GY-521: Acelerometro y Giroscopio MPU-6050 Board GY-521
  LCD screen 16x2 IIC: LCD screen with HD44780 controller enables showing text, symbols, value or anything else that comes from Croduino/Arduino. It is capable of showing 16 symbols in two lines and therefore can be used in many projects that need to send clearly visible and legible output information.. • Color of symbols: White • Backlight: Blue • Dimensions: 80 x 36 x 12 mm • Screen dimensions: 64.5 x 16 mm •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
